# Fritzing sketch 1 (saved by Fritzing 0.9.3b)
breadboards: 4

parts:
  VCC3 = Battery
  J77 = female pin header, 3 pins [form="♀ (female)"]
  J79 = female pin header, 3 pins [form="♀ (female)"]
  J80 = female pin header, 3 pins [form="♀ (female)"]  # not connected
  J81 = female pin header, 3 pins [form="♀ (female)"]  # not connected
  J83 = female pin header, 4 pins [form="♀ (female)"]
  J84 = female pin header, 5 pins [form="♀ (female)"]
  J85 = female pin header, 4 pins [form="♀ (female)"]
  J86 = female pin header, 4 pins [form="♀ (female)"]
  J88 = female pin header, 3 pins [form="♀ (female)"]
  J89 = female pin header, 2 pins [form="♀ (female)"]
  J90 = female pin header, 4 pins [form="♀ (female)"]
  J92 = female pin header, 3 pins [form="♀ (female)"]
  J93 = female pin header, 3 pins [form="♀ (female)"]  # not connected
  J97 = female pin header, 3 pins [form="♀ (female)"]
  R1 = Resistor [tolerance=±5% resistance=220 package=THT]
  R2 = Resistor [tolerance=±5% resistance=220 package=THT]
  C3 = Ceramic Capacitor [capacitance=100nF package="100 mil [THT, multilayer]"]
  SPKR1 = Loudspeaker
  R3 = Trimmer Potentiometer [maximum_resistance=10kΩ package=THT]
  C4 = Ceramic Capacitor [capacitance=100nF package="100 mil [THT, multilayer]"]
  C5 = Ceramic Capacitor [capacitance=100nF package="100 mil [THT, multilayer]"]
  Q1 = PNP-Transistor [package="TO92 [THT]"]

nets:
  N1: VCC3.-, J79.pin1, J85.pin1, J97.pin1, SPKR1.pin2, R3.leg2, C4.0, C4.1
  N2: VCC3.+, J92.pin1, Q1.E
  N3: J77.pin1, J84.pin4, J84.pin5, R2.Pin_1
  N4: J77.pin3, C5.0
  N5: J83.pin1, R1.Pin_0
  N6: J84.pin1, J90.pin1, R2.Pin_0
  N7: J85.pin4, C3.1, SPKR1.pin1
  N8: J86.pin1, J90.pin4
  N9: J86.pin2, Q1.B
  N10: J86.pin4, C3.0
  N11: J88.pin1, J88.pin3
  N12: J89.pin1, J89.pin2
  N13: J92.pin3, C5.1
  N14: J97.pin2, Q1.C
  N15: R1.Pin_1, R3.wiper
