# Fritzing sketch 9 (saved by Fritzing 0.9.3b)
breadboards: 1

parts:
  Q1 = PNP-Transistor [package="TO92 [THT]"]
  C1 = Ceramic Capacitor [capacitance=100nF package="100 mil [THT, multilayer]"]  # not connected
  R1 = Resistor [tolerance=±5% resistance=220 package=THT]
  C2 = Ceramic Capacitor [capacitance=100nF package="100 mil [THT, multilayer]"]
  C3 = Ceramic Capacitor [capacitance=100nF package="100 mil [THT, multilayer]"]
  VCC1 = Battery
  S1 = Pushbutton [package=THT]  # not connected
  R2 = Resistor [tolerance=±5% resistance=220 package=THT]  # not connected
  R3 = Resistor [tolerance=±5% resistance=220 package=THT]
  R4 = Resistor [tolerance=±5% resistance=220 package=THT]  # not connected
  C4 = Ceramic Capacitor [capacitance=100nF package="100 mil [THT, multilayer]"]  # not connected
  S2 = Pushbutton [package=THT]  # not connected
  SPKR1 = Loudspeaker
  S3 = Toggle Switch [package=THT]  # not connected
  L1 = Inductor [package="400 mil [THT]"]  # not connected
  L2 = Inductor [package="400 mil [THT]"]
  R5 = Trimmer Potentiometer [maximum_resistance=10kΩ package=THT]  # not connected

nets:
  N1: Q1.E, VCC1.+
  N2: Q1.B, C2.0, C2.1
  N3: R1.Pin_1, R3.Pin_0
  N4: C3.0, C3.1
  N5: SPKR1.pin1, L2.pin_0
  N6: SPKR1.pin2, L2.pin_1
