# Fritzing sketch 11 (1) (saved by Fritzing 0.9.3b)
breadboards: 5

parts:
  IC1 = PICAXE-20M [package=THT]  # not connected
  IC2 = PICAXE-14M [package=THT]  # not connected
  CD4048B1 = CD4048B [part_number=CD4048B package="DIP (Dual Inline) [THT]"]  # not connected
  U1 = MAX7219 [package=dil24]  # not connected
  IC3 = uM-FPUv2 [package=THT]  # not connected
  IC4 = PICAXE-20X2 [package=THT]  # not connected
  IC5 = 25LC020 [package=THT]
  IC6 = 4071 4 x 2 Input OR Gate, single part [part_number=4071 package="DIP (Dual Inline) [THT]"]  # not connected
  U2 = SN74LS32N [package="DIP14 [THT]"]  # not connected
  IC7 = 24LC01 [package=THT]  # not connected
  U3 = SN74LS20N [package="DIP14 [THT]"]  # not connected
  IC8 = FRM050 [package=THT]
  S1 = Pushbutton [package=THT]
  VCC1 = Battery
  C1 = Ceramic Capacitor [capacitance=100nF package="100 mil [THT, multilayer]"]
  J1 = female pin header, 2 pins [form="♀ (female)"]
  J33 = female pin header, 3 pins [form="♀ (female)"]
  J34 = female pin header, 5 pins [form="♀ (female)"]  # not connected
  J37 = female pin header, 4 pins [form="♀ (female)"]
  J40 = female pin header, 4 pins [form="♀ (female)"]  # not connected
  J43 = female pin header, 4 pins [form="♀ (female)"]
  J44 = female pin header, 3 pins [form="♀ (female)"]
  Q2 = PNP-Transistor [package="TO92 [THT]"]
  R8 = Resistor [tolerance=±5% resistance=220 package=THT]
  J45 = female pin header, 4 pins [form="♀ (female)"]
  J46 = female pin header, 3 pins [form="♀ (female)"]
  J47 = female pin header, 3 pins [form="♀ (female)"]
  J48 = female pin header, 4 pins [form="♀ (female)"]
  J49 = female pin header, 3 pins [form="♀ (female)"]
  J50 = female pin header, 3 pins [form="♀ (female)"]
  R9 = Resistor [tolerance=±5% resistance=220 package=THT]
  J51 = female pin header, 4 pins [form="♀ (female)"]
  J52 = female pin header, 2 pins [form="♀ (female)"]
  J53 = female pin header, 3 pins [form="♀ (female)"]
  J54 = female pin header, 3 pins [form="♀ (female)"]
  R10 = Resistor [tolerance=±5% resistance=220 package=THT]
  J55 = female pin header, 4 pins [form="♀ (female)"]
  J56 = female pin header, 4 pins [form="♀ (female)"]
  J57 = female pin header, 3 pins [form="♀ (female)"]
  J58 = female pin header, 3 pins [form="♀ (female)"]
  R11 = Resistor [tolerance=±5% resistance=220 package=THT]
  J59 = female pin header, 3 pins [form="♀ (female)"]
  J60 = female pin header, 3 pins [form="♀ (female)"]
  LED1 = LED - 5mm [color="Red (633nm)" package="5 mm [THT]"]
  J61 = female pin header, 4 pins [form="♀ (female)"]
  J62 = female pin header, 4 pins [form="♀ (female)"]
  J63 = female pin header, 3 pins [form="♀ (female)"]
  J64 = female pin header, 2 pins [form="♀ (female)"]
  J65 = female pin header, 2 pins [form="♀ (female)"]
  J66 = female pin header, 3 pins [form="♀ (female)"]
  J67 = female pin header, 3 pins [form="♀ (female)"]
  J68 = female pin header, 3 pins [form="♀ (female)"]
  J69 = female pin header, 3 pins [form="♀ (female)"]
  J71 = female pin header, 5 pins [form="♀ (female)"]  # not connected
  J72 = female pin header, 5 pins [form="♀ (female)"]  # not connected
  J73 = female pin header, 5 pins [form="♀ (female)"]  # not connected
  J74 = female pin header, 5 pins [form="♀ (female)"]  # not connected
  J75 = female pin header, 5 pins [form="♀ (female)"]  # not connected
  J76 = female pin header, 5 pins [form="♀ (female)"]  # not connected
  J77 = female pin header, 5 pins [form="♀ (female)"]  # not connected
  J78 = female pin header, 4 pins [form="♀ (female)"]
  J79 = female pin header, 4 pins [form="♀ (female)"]  # not connected
  J80 = female pin header, 4 pins [form="♀ (female)"]  # not connected
  J81 = female pin header, 5 pins [form="♀ (female)"]  # not connected
  J82 = female pin header, 3 pins [form="♀ (female)"]  # not connected
  J83 = female pin header, 3 pins [form="♀ (female)"]  # not connected
  J84 = female pin header, 3 pins [form="♀ (female)"]  # not connected
  J85 = female pin header, 3 pins [form="♀ (female)"]  # not connected
  J86 = female pin header, 3 pins [form="♀ (female)"]
  J87 = female pin header, 2 pins [form="♀ (female)"]
  J88 = female pin header, 2 pins [form="♀ (female)"]

nets:
  N1: IC5.+V, IC8.In_4
  N2: S1.leg0, VCC1.-, J48.pin1, J57.pin1, J58.pin1, R11.Pin_0, J59.pin1, J59.pin2, J59.pin3, J60.pin1, J60.pin2, J60.pin3, LED1.cathode, LED1.anode, J61.pin1, J61.pin4, J62.pin1, J62.pin4, J69.pin1, J69.pin3
  N3: S1.leg1, VCC1.+, C1.0, C1.1, J1.pin1, J1.pin2, J33.pin1, J33.pin3, J37.pin1, J37.pin2, J37.pin4, J43.pin1, J43.pin4, J44.pin1, J44.pin3, Q2.E, Q2.C, R8.Pin_0, R8.Pin_1, J45.pin1, J46.pin1, J46.pin2, J46.pin3, J47.pin1, J47.pin2, J47.pin3, J48.pin4, J49.pin1, J49.pin3, J50.pin1, J50.pin3, R9.Pin_0, R9.Pin_1, J51.pin1, J51.pin4, J52.pin1, J52.pin2, J55.pin1, J55.pin4, J56.pin1, J56.pin4, J63.pin1, J63.pin2, J63.pin3, J64.pin1, J64.pin2, J65.pin1, J65.pin2, J66.pin1, J66.pin3, J67.pin2, J68.pin3, J78.pin1, J78.pin4, J86.pin1, J86.pin2, J86.pin3, J87.pin1, J87.pin2, J88.pin1, J88.pin2
  N4: J33.pin2, J44.pin2, Q2.B, J53.pin1, J54.pin1, R10.Pin_0, J67.pin1, J67.pin3
  N5: J37.pin3, J49.pin2, J50.pin2
  N6: J45.pin2, J45.pin4, J53.pin3, J54.pin3, R10.Pin_1
  N7: J57.pin2, J58.pin2
  N8: J57.pin3, J58.pin3, R11.Pin_1, J68.pin1, J68.pin2
