# Fritzing sketch 12 (saved by Fritzing 0.9.3b)
breadboards: 4

parts:
  VCC3 = Battery
  J77 = female pin header, 3 pins [form="♀ (female)"]
  J78 = female pin header, 2 pins [form="♀ (female)"]
  J79 = female pin header, 3 pins [form="♀ (female)"]
  J80 = female pin header, 3 pins [form="♀ (female)"]
  J81 = female pin header, 3 pins [form="♀ (female)"]
  Q2 = NPN-Transistor [package="TO92 [THT]"]
  J82 = female pin header, 2 pins [form="♀ (female)"]
  J84 = female pin header, 5 pins [form="♀ (female)"]
  J85 = female pin header, 4 pins [form="♀ (female)"]
  J86 = female pin header, 4 pins [form="♀ (female)"]
  C2 = Ceramic Capacitor [capacitance=100nF package="100 mil [THT, multilayer]"]
  LED4 = LED - 5mm [color="Red (633nm)" package="5 mm [THT]"]
  J87 = female pin header, 4 pins [form="♀ (female)"]
  J88 = female pin header, 3 pins [form="♀ (female)"]
  J89 = female pin header, 2 pins [form="♀ (female)"]
  J90 = female pin header, 4 pins [form="♀ (female)"]
  S3 = Pushbutton [package=THT]
  J91 = female pin header, 3 pins [form="♀ (female)"]
  J92 = female pin header, 3 pins [form="♀ (female)"]
  R13 = Resistor [tolerance=±5% resistance=220 package=THT]
  J93 = female pin header, 3 pins [form="♀ (female)"]
  J94 = female pin header, 3 pins [form="♀ (female)"]
  R14 = Resistor [tolerance=±5% resistance=220 package=THT]
  L1 = Inductor [package="400 mil [THT]"]
  J95 = female pin header, 3 pins [form="♀ (female)"]
  J96 = female pin header, 3 pins [form="♀ (female)"]
  J97 = female pin header, 3 pins [form="♀ (female)"]
  J98 = female pin header, 3 pins [form="♀ (female)"]
  L2 = Inductor [package="400 mil [THT]"]

nets:
  N1: VCC3.-, J78.pin1, J78.pin2, C2.1, L1.pin_0, L1.pin_1, J95.pin2, J96.pin2
  N2: VCC3.+, J86.pin1, J86.pin4, J91.pin3, J92.pin3, R13.Pin_0
  N3: J77.pin2, Q2.B
  N4: J79.pin1, Q2.E
  N5: J79.pin3, Q2.C
  N6: J80.pin2, LED4.cathode
  N7: J81.pin1, LED4.anode
  N8: J82.pin1, J82.pin2, C2.0, J90.pin4, S3.leg1, J91.pin1, J92.pin1, R13.Pin_1
  N9: J84.pin1, J84.pin5
  N10: J85.pin1, J85.pin4
  N11: J87.pin1, J87.pin4
  N12: J88.pin1, J88.pin3
  N13: J89.pin1, J89.pin2
  N14: J90.pin1, S3.leg0, J95.pin3, J96.pin3
  N15: J91.pin2, J92.pin2
  N16: J93.pin1, R14.Pin_0
  N17: J94.pin3, R14.Pin_1
  N18: J95.pin1, J96.pin1
  N19: J97.pin1, J98.pin1
  N20: J97.pin2, J98.pin2, L2.pin_0, L2.pin_1
  N21: J97.pin3, J98.pin3
