# Fritzing sketch 15 (1) (saved by Fritzing 0.9.3b)
breadboards: 5

parts:
  IC9 = PICAXE-20M [package=THT]  # not connected
  IC10 = PICAXE-14M [package=THT]  # not connected
  CD4048B2 = CD4048B [part_number=CD4048B package="DIP (Dual Inline) [THT]"]  # not connected
  U4 = MAX7219 [package=dil24]  # not connected
  IC11 = uM-FPUv2 [package=THT]  # not connected
  IC12 = PICAXE-20X2 [package=THT]  # not connected
  IC13 = 25LC020 [package=THT]
  IC14 = 4071 4 x 2 Input OR Gate, single part [part_number=4071 package="DIP (Dual Inline) [THT]"]  # not connected
  U5 = SN74LS32N [package="DIP14 [THT]"]  # not connected
  IC15 = 24LC01 [package=THT]  # not connected
  U6 = SN74LS20N [package="DIP14 [THT]"]  # not connected
  IC16 = FRM050 [package=THT]
  VCC2 = Battery
  J48 = female pin header, 3 pins [form="♀ (female)"]
  J49 = female pin header, 2 pins [form="♀ (female)"]
  R9 = Resistor [tolerance=±5% resistance=220 package=THT]
  J54 = female pin header, 4 pins [form="♀ (female)"]
  J55 = female pin header, 4 pins [form="♀ (female)"]
  J57 = female pin header, 4 pins [form="♀ (female)"]
  J58 = female pin header, 4 pins [form="♀ (female)"]
  J59 = female pin header, 4 pins [form="♀ (female)"]
  R10 = Resistor [tolerance=±5% resistance=220 package=THT]
  S2 = Pushbutton [package=THT]
  R11 = Resistor [tolerance=±5% resistance=220 package=THT]
  J60 = female pin header, 3 pins [form="♀ (female)"]
  R12 = Resistor [tolerance=±5% resistance=220 package=THT]
  J62 = female pin header, 3 pins [form="♀ (female)"]
  J63 = female pin header, 3 pins [form="♀ (female)"]
  Q1 = NPN-Transistor [package="TO92 [THT]"]
  C1 = Ceramic Capacitor [capacitance=100nF package="100 mil [THT, multilayer]"]
  J64 = female pin header, 2 pins [form="♀ (female)"]
  J65 = female pin header, 4 pins [form="♀ (female)"]
  J66 = female pin header, 5 pins [form="♀ (female)"]
  J67 = female pin header, 4 pins [form="♀ (female)"]
  J68 = female pin header, 4 pins [form="♀ (female)"]
  LED3 = LED - 5mm [color="Red (633nm)" package="5 mm [THT]"]
  J69 = female pin header, 4 pins [form="♀ (female)"]
  J70 = female pin header, 3 pins [form="♀ (female)"]
  J71 = female pin header, 2 pins [form="♀ (female)"]
  J72 = female pin header, 4 pins [form="♀ (female)"]
  J73 = female pin header, 3 pins [form="♀ (female)"]
  J74 = female pin header, 3 pins [form="♀ (female)"]
  J75 = female pin header, 3 pins [form="♀ (female)"]
  J76 = female pin header, 3 pins [form="♀ (female)"]

nets:
  N1: IC13.+V, IC16.In_4
  N2: VCC2.-, R12.Pin_1, C1.0, J64.pin1, J64.pin2, J75.pin3, J76.pin3
  N3: VCC2.+, J48.pin3, S2.leg1, J60.pin3, Q1.C, J65.pin1, J65.pin3, J65.pin4, J66.pin4, J66.pin5, J69.pin1, J69.pin4, J70.pin1, J70.pin3, J71.pin1, J71.pin2, J72.pin4
  N4: J48.pin1, J60.pin1, Q1.E
  N5: J48.pin2, J49.pin1, J49.pin2, R9.Pin_0, J60.pin2, Q1.B, C1.1, J67.pin1, J67.pin4, J73.pin3, J74.pin3
  N6: R9.Pin_1, S2.leg0, J72.pin1, J73.pin1, J73.pin2, J74.pin1, J74.pin2
  N7: J54.pin1, R10.Pin_0
  N8: J55.pin4, R11.Pin_1
  N9: J57.pin1, R11.Pin_0
  N10: J58.pin3, J58.pin4, R10.Pin_1
  N11: J59.pin1, J59.pin4
  N12: R12.Pin_0, J62.pin2, J63.pin2, LED3.cathode, J75.pin1, J76.pin1
  N13: J62.pin1, J63.pin1, J66.pin1, J68.pin1, J68.pin4, LED3.anode
  N14: J62.pin3, J63.pin3
  N15: J75.pin2, J76.pin2
