# Fritzing sketch 16 (saved by Fritzing 0.9.3b)
breadboards: 4

parts:
  VCC3 = Battery
  J77 = female pin header, 3 pins [form="♀ (female)"]
  J78 = female pin header, 2 pins [form="♀ (female)"]
  J79 = female pin header, 3 pins [form="♀ (female)"]
  J80 = female pin header, 3 pins [form="♀ (female)"]
  J81 = female pin header, 3 pins [form="♀ (female)"]
  J82 = female pin header, 2 pins [form="♀ (female)"]
  J83 = female pin header, 4 pins [form="♀ (female)"]
  J84 = female pin header, 5 pins [form="♀ (female)"]
  J85 = female pin header, 4 pins [form="♀ (female)"]
  J86 = female pin header, 4 pins [form="♀ (female)"]
  C2 = Ceramic Capacitor [capacitance=100nF package="100 mil [THT, multilayer]"]
  LED4 = LED - 5mm [color="Red (633nm)" package="5 mm [THT]"]
  J87 = female pin header, 4 pins [form="♀ (female)"]
  J88 = female pin header, 3 pins [form="♀ (female)"]
  J89 = female pin header, 2 pins [form="♀ (female)"]
  J90 = female pin header, 4 pins [form="♀ (female)"]
  S3 = Pushbutton [package=THT]
  J91 = female pin header, 3 pins [form="♀ (female)"]
  J92 = female pin header, 3 pins [form="♀ (female)"]
  R13 = Resistor [tolerance=±5% resistance=220 package=THT]
  J93 = female pin header, 3 pins [form="♀ (female)"]
  J94 = female pin header, 3 pins [form="♀ (female)"]
  R14 = Resistor [tolerance=±5% resistance=220 package=THT]
  Q3 = PNP-Transistor [package="TO92 [THT]"]
  Q4 = NPN-Transistor [package="TO92 [THT]"]
  J95 = female pin header, 3 pins [form="♀ (female)"]
  J96 = female pin header, 3 pins [form="♀ (female)"]
  LED5 = LED - 5mm [color="Red (633nm)" package="5 mm [THT]"]  # not connected
  J97 = female pin header, 3 pins [form="♀ (female)"]
  J98 = female pin header, 3 pins [form="♀ (female)"]
  R15 = Resistor [tolerance=±5% resistance=220 package=THT]
  J99 = female pin header, 4 pins [form="♀ (female)"]

nets:
  N1: VCC3.-, J90.pin1, S3.leg0, Q4.C, J95.pin1, J96.pin1
  N2: VCC3.+, J77.pin3, J79.pin3, J86.pin1, J86.pin4, J87.pin1, J87.pin4, Q3.E
  N3: J77.pin1, J79.pin1, J80.pin1, J81.pin1, LED4.anode, Q3.C
  N4: J77.pin2, J79.pin2, J91.pin1, J91.pin2, J92.pin1, J92.pin2, R13.Pin_1, Q3.B, J99.pin1, J99.pin4
  N5: J78.pin1, C2.1
  N6: J80.pin2, J81.pin2, J85.pin1, J85.pin4, LED4.cathode, J97.pin1, J98.pin1, R15.Pin_1
  N7: J80.pin3, J81.pin3
  N8: J82.pin2, C2.0
  N9: J83.pin1, J83.pin3, J83.pin4, J93.pin1, J94.pin1, R14.Pin_1, Q4.B, J95.pin2, J96.pin2
  N10: J84.pin1, J84.pin5
  N11: J88.pin1, J88.pin3
  N12: J89.pin1, J89.pin2
  N13: J90.pin4, S3.leg1, J91.pin3, J92.pin3, R13.Pin_0
  N14: J93.pin2, J94.pin2
  N15: J93.pin3, J94.pin3, R14.Pin_0
  N16: Q4.E, J95.pin3, J96.pin3, J97.pin3, J98.pin3, R15.Pin_0
  N17: J97.pin2, J98.pin2
