# Fritzing sketch 21 (saved by Fritzing 0.9.3b)
breadboards: 5

parts:
  J14 = female pin header, 3 pins [form="♀ (female)"]
  J15 = female pin header, 3 pins [form="♀ (female)"]
  J24 = female pin header, 3 pins [form="♀ (female)"]
  J25 = female pin header, 3 pins [form="♀ (female)"]
  C2 = Ceramic Capacitor [capacitance=100nF package="100 mil [THT, multilayer]"]
  J26 = female pin header, 3 pins [form="♀ (female)"]
  J27 = female pin header, 3 pins [form="♀ (female)"]
  C3 = Ceramic Capacitor [capacitance=100nF package="100 mil [THT, multilayer]"]
  J32 = female pin header, 5 pins [form="♀ (female)"]
  Q1 = PNP-Transistor [package="TO92 [THT]"]
  D1 = Rectifier Diode [part_number=1N4001 package="300 mil [THT]"]  # not connected
  J33 = female pin header, 3 pins [form="♀ (female)"]
  J34 = female pin header, 3 pins [form="♀ (female)"]
  D2 = Rectifier Diode [part_number=1N4001 package="300 mil [THT]"]
  J35 = female pin header, 3 pins [form="♀ (female)"]
  J36 = female pin header, 3 pins [form="♀ (female)"]
  D3 = Rectifier Diode [part_number=1N4001 package="300 mil [THT]"]
  J37 = female pin header, 3 pins [form="♀ (female)"]
  J39 = female pin header, 4 pins [form="♀ (female)"]
  R1 = Resistor [tolerance=±5% resistance=10k package=THT]
  J40 = female pin header, 3 pins [form="♀ (female)"]
  J41 = female pin header, 3 pins [form="♀ (female)"]
  R2 = Resistor [tolerance=±5% resistance=10k package=THT]
  J42 = female pin header, 3 pins [form="♀ (female)"]
  J43 = female pin header, 4 pins [form="♀ (female)"]
  J44 = female pin header, 4 pins [form="♀ (female)"]
  J45 = female pin header, 3 pins [form="♀ (female)"]
  J46 = female pin header, 3 pins [form="♀ (female)"]
  J47 = female pin header, 4 pins [form="♀ (female)"]
  J48 = female pin header, 3 pins [form="♀ (female)"]
  J49 = female pin header, 3 pins [form="♀ (female)"]
  R3 = Resistor [tolerance=±5% resistance=470 package=THT]
  D4 = Rectifier Diode [part_number=1N4001 package="300 mil [THT]"]
  J51 = female pin header, 3 pins [form="♀ (female)"]
  J53 = female pin header, 3 pins [form="♀ (female)"]
  J54 = female pin header, 3 pins [form="♀ (female)"]
  R4 = Resistor [tolerance=±5% resistance=22k package=THT]
  J55 = female pin header, 4 pins [form="♀ (female)"]
  J56 = female pin header, 4 pins [form="♀ (female)"]
  J57 = female pin header, 4 pins [form="♀ (female)"]
  Q2 = NPN-Transistor [package="TO92 [THT]"]
  J58 = female pin header, 3 pins [form="♀ (female)"]
  J59 = female pin header, 3 pins [form="♀ (female)"]
  LED1 = LED - 5mm [color="Red (633nm)" package="5 mm [THT]"]
  J60 = female pin header, 3 pins [form="♀ (female)"]
  J61 = female pin header, 3 pins [form="♀ (female)"]
  J62 = female pin header, 4 pins [form="♀ (female)"]
  J63 = female pin header, 3 pins [form="♀ (female)"]
  J64 = female pin header, 5 pins [form="♀ (female)"]
  J65 = female pin header, 3 pins [form="♀ (female)"]
  J66 = female pin header, 5 pins [form="♀ (female)"]
  J67 = female pin header, 4 pins [form="♀ (female)"]
  J69 = female pin header, 3 pins [form="♀ (female)"]
  J70 = female pin header, 3 pins [form="♀ (female)"]
  J71 = female pin header, 3 pins [form="♀ (female)"]
  J72 = female pin header, 3 pins [form="♀ (female)"]
  J73 = female pin header, 3 pins [form="♀ (female)"]
  R5 = Resistor [tolerance=±5% resistance=220 package=THT]
  J74 = female pin header, 4 pins [form="♀ (female)"]
  J75 = female pin header, 3 pins [form="♀ (female)"]
  J76 = female pin header, 3 pins [form="♀ (female)"]
  Q3 = PNP-Transistor [package="TO92 [THT]"]  # not connected
  J77 = female pin header, 3 pins [form="♀ (female)"]
  J78 = female pin header, 3 pins [form="♀ (female)"]
  J79 = female pin header, 5 pins [form="♀ (female)"]
  J80 = female pin header, 4 pins [form="♀ (female)"]
  J81 = female pin header, 4 pins [form="♀ (female)"]
  J82 = female pin header, 3 pins [form="♀ (female)"]
  J83 = female pin header, 3 pins [form="♀ (female)"]
  J84 = female pin header, 3 pins [form="♀ (female)"]

nets:
  N1: J14.pin1, J14.pin2, J14.pin3, R1.Pin_1
  N2: J15.pin1, J15.pin2, J15.pin3, R1.Pin_0, Q2.B, J58.pin2, J59.pin2, J67.pin1, J67.pin4
  N3: J24.pin3, C2.1
  N4: J25.pin1, C2.0
  N5: J26.pin3, C3.1
  N6: J27.pin1, C3.0
  N7: J32.pin1, J32.pin5
  N8: Q1.E, Q1.C, J45.pin1, J46.pin1, D4.cathode, J70.pin1, J70.pin3, J71.pin1, J71.pin3, J76.pin2, J79.pin1, J79.pin5, J82.pin2, J83.pin1, J83.pin3
  N9: Q1.B, J33.pin1, J34.pin1, D2.cathode, J35.pin3, J36.pin3, D3.cathode, J37.pin1, J37.pin3, J39.pin1, J39.pin4, J41.pin1, J41.pin2, J41.pin3, R2.Pin_1, J42.pin1, J42.pin2, J42.pin3, J51.pin1, J51.pin3, J70.pin2, J71.pin2, J76.pin1, J76.pin3, J80.pin1, J80.pin4, J81.pin1, J81.pin4, J82.pin1, J82.pin3, J83.pin2
  N10: J33.pin2, J34.pin2, J39.pin3
  N11: J33.pin3, J34.pin3, D2.anode, J39.pin2
  N12: J35.pin1, J36.pin1, D3.anode
  N13: J35.pin2, J36.pin2
  N14: J40.pin1, J40.pin2, J40.pin3, R2.Pin_0, J43.pin1, J43.pin4, J44.pin1, J44.pin4, J45.pin3, J46.pin3, J47.pin1, J47.pin4, J48.pin3, J49.pin3, R3.Pin_0, D4.anode, J55.pin1, J55.pin4
  N15: J45.pin2, J46.pin2
  N16: J48.pin1, J49.pin1, R3.Pin_1, J57.pin1, J57.pin4, LED1.anode, J60.pin3, J61.pin3, J78.pin1, J78.pin3
  N17: J48.pin2, J49.pin2
  N18: J53.pin1, J53.pin2, J53.pin3, R4.Pin_0, J56.pin1, J56.pin4, Q2.E, J58.pin1, J59.pin1, J65.pin1, J65.pin3, J66.pin1, J66.pin5, J84.pin1, J84.pin3
  N19: J54.pin1, J54.pin2, J54.pin3, R4.Pin_1, J69.pin1, J69.pin3
  N20: Q2.C, J58.pin3, J59.pin3, LED1.cathode, J60.pin1, J61.pin1, J63.pin1, J63.pin3, J64.pin1, J64.pin5, J77.pin1, J77.pin3
  N21: J60.pin2, J61.pin2
  N22: J62.pin1, J62.pin4
  N23: J72.pin1, R5.Pin_0
  N24: J73.pin3, R5.Pin_1
  N25: J74.pin1, J74.pin4, J81.pin3
  N26: J75.pin1, J75.pin3

// code stored in the sketch: ⁿ║√╣¬°≥°±¿≡¬■¿.ino

