# Fritzing sketch 22 (saved by Fritzing 0.9.3b)
breadboards: 5

parts:
  Q1 = PNP-Transistor [package="TO92 [THT]"]
  J33 = female pin header, 3 pins [form="♀ (female)"]
  J34 = female pin header, 3 pins [form="♀ (female)"]
  D2 = Rectifier Diode [part_number=1N4001 package="300 mil [THT]"]
  J35 = female pin header, 3 pins [form="♀ (female)"]
  J36 = female pin header, 3 pins [form="♀ (female)"]
  D3 = Rectifier Diode [part_number=1N4001 package="300 mil [THT]"]
  J37 = female pin header, 3 pins [form="♀ (female)"]
  J39 = female pin header, 4 pins [form="♀ (female)"]
  J40 = female pin header, 3 pins [form="♀ (female)"]
  J41 = female pin header, 3 pins [form="♀ (female)"]
  R2 = Resistor [tolerance=±5% resistance=4.7k package=THT]
  J43 = female pin header, 4 pins [form="♀ (female)"]
  J44 = female pin header, 4 pins [form="♀ (female)"]
  J47 = female pin header, 4 pins [form="♀ (female)"]
  J48 = female pin header, 3 pins [form="♀ (female)"]
  J49 = female pin header, 3 pins [form="♀ (female)"]
  R3 = Resistor [tolerance=±5% resistance=22k package=THT]
  J51 = female pin header, 3 pins [form="♀ (female)"]
  J55 = female pin header, 4 pins [form="♀ (female)"]
  J56 = female pin header, 4 pins [form="♀ (female)"]
  J57 = female pin header, 4 pins [form="♀ (female)"]
  Q2 = NPN-Transistor [package="TO92 [THT]"]
  J58 = female pin header, 3 pins [form="♀ (female)"]
  J59 = female pin header, 3 pins [form="♀ (female)"]
  J60 = female pin header, 3 pins [form="♀ (female)"]
  J61 = female pin header, 3 pins [form="♀ (female)"]
  J62 = female pin header, 4 pins [form="♀ (female)"]
  J64 = female pin header, 5 pins [form="♀ (female)"]
  J66 = female pin header, 5 pins [form="♀ (female)"]
  J69 = female pin header, 3 pins [form="♀ (female)"]
  J70 = female pin header, 3 pins [form="♀ (female)"]
  J71 = female pin header, 3 pins [form="♀ (female)"]
  J72 = female pin header, 3 pins [form="♀ (female)"]
  J73 = female pin header, 3 pins [form="♀ (female)"]
  R5 = Resistor [tolerance=±5% resistance=10k package=THT]
  J74 = female pin header, 4 pins [form="♀ (female)"]
  J75 = female pin header, 3 pins [form="♀ (female)"]
  J77 = female pin header, 3 pins [form="♀ (female)"]
  J79 = female pin header, 5 pins [form="♀ (female)"]
  J80 = female pin header, 4 pins [form="♀ (female)"]
  J87 = female pin header, 5 pins [form="♀ (female)"]
  J88 = female pin header, 4 pins [form="♀ (female)"]
  J90 = female pin header, 4 pins [form="♀ (female)"]
  J92 = female pin header, 4 pins [form="♀ (female)"]
  J93 = female pin header, 4 pins [form="♀ (female)"]
  J95 = female pin header, 4 pins [form="♀ (female)"]
  LED1 = LED - 5mm [color="Red (633nm)" package="5 mm [THT]"]
  J96 = female pin header, 3 pins [form="♀ (female)"]
  J97 = female pin header, 3 pins [form="♀ (female)"]
  R6 = Resistor [tolerance=±5% resistance=10k package=THT]
  J98 = female pin header, 3 pins [form="♀ (female)"]
  J99 = female pin header, 3 pins [form="♀ (female)"]
  R7 = Resistor [tolerance=±5% resistance=470 package=THT]
  J100 = female pin header, 5 pins [form="♀ (female)"]

nets:
  N1: Q1.E, J55.pin1, J55.pin4, J57.pin1, J57.pin4, J60.pin1, J61.pin1, J64.pin1, J64.pin5, J70.pin1, J71.pin1, J77.pin1, J77.pin3, J92.pin1, J92.pin4, LED1.cathode
  N2: Q1.B, J41.pin1, J41.pin2, J41.pin3, R2.Pin_1, J66.pin1, J66.pin2, J66.pin4, J66.pin5, J70.pin2, J71.pin2, J73.pin1, J73.pin2, J73.pin3, R5.Pin_1, J93.pin1, J93.pin4
  N3: Q1.C, J70.pin3, J71.pin3, J74.pin1, J74.pin4, J90.pin1, J90.pin4, J97.pin1, J97.pin2, J97.pin3, R6.Pin_1
  N4: J33.pin1, J34.pin1, D2.cathode, J35.pin3, J36.pin3, D3.cathode, J37.pin1, J37.pin3, J39.pin1, J39.pin4, J51.pin1, J51.pin3, J72.pin1, J72.pin2, J72.pin3, R5.Pin_0, J75.pin1, J75.pin3, J80.pin1, J80.pin4, J88.pin1, J88.pin4
  N5: J33.pin2, J34.pin2, J39.pin3
  N6: J33.pin3, J34.pin3, D2.anode, J39.pin2
  N7: J35.pin1, J36.pin1, D3.anode
  N8: J35.pin2, J36.pin2
  N9: J40.pin1, J40.pin2, J40.pin3, R2.Pin_0, J43.pin1, J43.pin4
  N10: J44.pin1, J44.pin4
  N11: J47.pin1, J47.pin4, J48.pin1, J48.pin2, J48.pin3, R3.Pin_0, J56.pin1, J56.pin4, Q2.E, Q2.C, J58.pin1, J58.pin3, J59.pin1, J59.pin3, J69.pin1, J69.pin3, J79.pin2, J79.pin4, J98.pin1, J98.pin2, J98.pin3, R7.Pin_0
  N12: J49.pin1, J49.pin2, J49.pin3, R3.Pin_1, Q2.B, J58.pin2, J59.pin2, J62.pin1, J62.pin3, J62.pin4, J79.pin1, J79.pin5, J95.pin1, J95.pin4, J96.pin1, J96.pin2, J96.pin3, R6.Pin_0
  N13: J60.pin2, J60.pin3, J61.pin2, J61.pin3, J87.pin1, J87.pin4, J87.pin5, LED1.anode, J99.pin1, J99.pin2, J99.pin3, R7.Pin_1, J100.pin1, J100.pin5
  N14: J69.pin2, J79.pin3

// code stored in the sketch: ªµvµ·-Ω-¼°Φ·µ°.ino

