# Fritzing sketch 23 (saved by Fritzing 0.9.3b)
breadboards: 5

parts:
  Q1 = PNP-Transistor [package="TO92 [THT]"]
  J33 = female pin header, 3 pins [form="♀ (female)"]
  J34 = female pin header, 3 pins [form="♀ (female)"]
  D2 = Rectifier Diode [part_number=1N4001 package="300 mil [THT]"]
  J35 = female pin header, 3 pins [form="♀ (female)"]
  J36 = female pin header, 3 pins [form="♀ (female)"]
  D3 = Rectifier Diode [part_number=1N4001 package="300 mil [THT]"]
  J37 = female pin header, 3 pins [form="♀ (female)"]
  J39 = female pin header, 4 pins [form="♀ (female)"]
  J43 = female pin header, 4 pins [form="♀ (female)"]
  J44 = female pin header, 4 pins [form="♀ (female)"]
  J45 = female pin header, 3 pins [form="♀ (female)"]
  J46 = female pin header, 3 pins [form="♀ (female)"]
  J47 = female pin header, 4 pins [form="♀ (female)"]
  D4 = Rectifier Diode [part_number=1N4001 package="300 mil [THT]"]
  J51 = female pin header, 3 pins [form="♀ (female)"]
  J55 = female pin header, 4 pins [form="♀ (female)"]
  J57 = female pin header, 4 pins [form="♀ (female)"]
  J60 = female pin header, 3 pins [form="♀ (female)"]
  J61 = female pin header, 3 pins [form="♀ (female)"]
  J62 = female pin header, 4 pins [form="♀ (female)"]
  J65 = female pin header, 3 pins [form="♀ (female)"]
  J69 = female pin header, 3 pins [form="♀ (female)"]
  J70 = female pin header, 3 pins [form="♀ (female)"]
  J71 = female pin header, 3 pins [form="♀ (female)"]
  J74 = female pin header, 4 pins [form="♀ (female)"]
  J75 = female pin header, 3 pins [form="♀ (female)"]
  J80 = female pin header, 4 pins [form="♀ (female)"]
  J82 = female pin header, 3 pins [form="♀ (female)"]
  J87 = female pin header, 5 pins [form="♀ (female)"]
  J92 = female pin header, 4 pins [form="♀ (female)"]
  LED1 = LED - 5mm [color="Red (633nm)" package="5 mm [THT]"]
  J96 = female pin header, 3 pins [form="♀ (female)"]
  J97 = female pin header, 3 pins [form="♀ (female)"]
  R6 = Resistor [tolerance=±5% resistance=10k package=THT]
  J98 = female pin header, 3 pins [form="♀ (female)"]
  J99 = female pin header, 3 pins [form="♀ (female)"]
  R7 = Resistor [tolerance=±5% resistance=470 package=THT]

nets:
  N1: Q1.E, J45.pin3, J46.pin3, D4.anode, J55.pin1, J55.pin4, J62.pin1, J62.pin4, J70.pin1, J71.pin1
  N2: Q1.B, J33.pin1, J34.pin1, D2.anode, J35.pin3, J36.pin3, D3.anode, J37.pin1, J37.pin3, J39.pin1, J39.pin4, J51.pin1, J51.pin3, J57.pin1, J57.pin4, J69.pin1, J69.pin3, J70.pin2, J71.pin2, J74.pin1, J74.pin2, J74.pin4, J75.pin1, J75.pin3, J80.pin1, J80.pin4, J97.pin1, J97.pin2, J97.pin3, R6.Pin_1
  N3: Q1.C, J70.pin3, J71.pin3, J87.pin1, J87.pin4, J87.pin5, J99.pin1, J99.pin2, J99.pin3, R7.Pin_1
  N4: J33.pin2, J34.pin2, J39.pin3
  N5: J33.pin3, J34.pin3, D2.cathode, J39.pin2
  N6: J35.pin1, J36.pin1, D3.cathode
  N7: J35.pin2, J36.pin2
  N8: J43.pin1, J43.pin4, J45.pin1, J46.pin1, D4.cathode, J92.pin1, J92.pin4
  N9: J44.pin1, J44.pin4, J65.pin1, J65.pin3, J96.pin1, J96.pin2, J96.pin3, R6.Pin_0
  N10: J45.pin2, J46.pin2
  N11: J47.pin1, J47.pin4, J60.pin2, J60.pin3, J61.pin2, J61.pin3, LED1.anode
  N12: J60.pin1, J61.pin1, J82.pin1, J82.pin3, LED1.cathode, J98.pin1, J98.pin2, J98.pin3, R7.Pin_0

// code stored in the sketch: ╣ªvªΩ░¬░╕Φ¿ΩªΦ.ino

