# Fritzing sketch 25 (saved by Fritzing 0.9.3b)
breadboards: 5

parts:
  Q1 = PNP-Transistor [package="TO92 [THT]"]
  J37 = female pin header, 3 pins [form="♀ (female)"]
  J43 = female pin header, 4 pins [form="♀ (female)"]
  J44 = female pin header, 4 pins [form="♀ (female)"]
  J57 = female pin header, 4 pins [form="♀ (female)"]
  J60 = female pin header, 3 pins [form="♀ (female)"]
  J61 = female pin header, 3 pins [form="♀ (female)"]
  J62 = female pin header, 4 pins [form="♀ (female)"]
  J65 = female pin header, 3 pins [form="♀ (female)"]
  J70 = female pin header, 3 pins [form="♀ (female)"]
  J71 = female pin header, 3 pins [form="♀ (female)"]
  J82 = female pin header, 3 pins [form="♀ (female)"]
  J87 = female pin header, 5 pins [form="♀ (female)"]
  LED1 = LED - 5mm [color="Red (633nm)" package="5 mm [THT]"]
  J98 = female pin header, 3 pins [form="♀ (female)"]
  J99 = female pin header, 3 pins [form="♀ (female)"]
  R7 = Resistor [tolerance=±5% resistance=470 package=THT]
  J15 = female pin header, 3 pins [form="♀ (female)"]
  J48 = female pin header, 3 pins [form="♀ (female)"]
  R1 = Resistor [tolerance=±5% resistance=10k package=THT]
  R3 = Resistor [tolerance=±5% resistance=10k package=THT]
  J14 = female pin header, 3 pins [form="♀ (female)"]
  J49 = female pin header, 3 pins [form="♀ (female)"]

nets:
  N1: Q1.E, J37.pin1, J37.pin3, J43.pin1, J43.pin4, J44.pin1, J44.pin4, J60.pin2, J60.pin3, J61.pin2, J61.pin3, J70.pin1, J71.pin1, LED1.anode
  N2: Q1.B, J57.pin1, J57.pin4, J65.pin1, J65.pin2, J65.pin3, J70.pin2, J71.pin2, J87.pin1, J87.pin2, J87.pin5, J15.pin1, J48.pin3, R1.Pin_0, R3.Pin_0, J14.pin1, J49.pin3
  N3: Q1.C, J62.pin1, J62.pin3, J62.pin4, J70.pin3, J71.pin3, J99.pin1, J99.pin2, J99.pin3, R7.Pin_1
  N4: J60.pin1, J61.pin1, J82.pin1, J82.pin3, LED1.cathode, J98.pin1, J98.pin2, J98.pin3, R7.Pin_0
  N5: J87.pin3, J48.pin1, R3.Pin_1, J49.pin1
  N6: J87.pin4, J48.pin2, J49.pin2
  N7: J15.pin2, J14.pin2
  N8: J15.pin3, R1.Pin_1, J14.pin3

// code stored in the sketch: ╣ªvªΩ░¬░╕Φ¿ΩªΦ.ino

